# Fritzing sketch Sketch (saved by Fritzing 0.9.3b)
circuit board: 9.9444cm x 3.84002cm
breadboards: 1

parts:
  R1 = Resistor [tolerance=±5% resistance=470 package=THT]
  J5 = female pin header, 4 pins [form="♀ (female)"]
  J6 = female pin header, 4 pins [form="♀ (female)"]
  R2 = Resistor [tolerance=±5% resistance=470 package=THT]
  R3 = Resistor [tolerance=±5% resistance=470 package=THT]
  R4 = Resistor [tolerance=±5% resistance=470 package=THT]
  R5 = Resistor [tolerance=±5% resistance=470 package=THT]
  R6 = Resistor [tolerance=±5% resistance=470 package=THT]
  R8 = Resistor [tolerance=±5% resistance=10k package=THT]
  R7 = Resistor [tolerance=±5% resistance=10k package=THT]
  R9 = Resistor [tolerance=±5% resistance=10k package=THT]
  R10 = Resistor [tolerance=±5% resistance=10k package=THT]
  R11 = Resistor [tolerance=±5% resistance=10k package=THT]
  R12 = Resistor [tolerance=±5% resistance=10k package=THT]
  J4 = female pin header, 4 pins [form="♀ (female)"]
  J3 = female pin header, 4 pins [form="♀ (female)"]
  J2 = female pin header, 4 pins [form="♀ (female)"]
  J1 = female pin header, 4 pins [form="♀ (female)"]
  J7 = female pin header, 10 pins [form="♀ (female)"]
  J8 = female pin header, 2 pins [form="♀ (female)"]

nets:
  N1: R1.Pin_0, R2.Pin_0, R3.Pin_0, R4.Pin_0, R5.Pin_0, R6.Pin_1, J7.pin10
  N2: R1.Pin_1, J1.pin1
  N3: J5.pin1, R3.Pin_1
  N4: J5.pin2, J5.pin3, J6.pin2, J6.pin3, J6.pin4, R12.Pin_0, J4.pin2, J4.pin3, J3.pin2, J3.pin3, J2.pin2, J2.pin3, J1.pin2, J1.pin3, J7.pin6, J7.pin7, J8.pin1
  N5: J5.pin4, R11.Pin_0, J7.pin5
  N6: J6.pin1, R4.Pin_1
  N7: R2.Pin_1, J2.pin1
  N8: R5.Pin_1, J4.pin1
  N9: R6.Pin_0, J3.pin1
  N10: R8.Pin_0, J2.pin4, J7.pin2
  N11: R8.Pin_1, R7.Pin_1, R9.Pin_1, R10.Pin_1, R11.Pin_1, R12.Pin_1, J7.pin8, J7.pin9, J8.pin2
  N12: R7.Pin_0, J1.pin4, J7.pin1
  N13: R9.Pin_0, J3.pin4, J7.pin3
  N14: R10.Pin_0, J4.pin4, J7.pin4
